# Fritzing sketch 4x4Key (saved by Fritzing 0.9.3b)
circuit board: 8.46667cm x 5.64444cm
perfboards: 1

parts:
  S5 = SWITCH-MOMENTARY-2 [package=tactile-switch-1101ne]
  S13 = SWITCH-MOMENTARY-2 [package=tactile-switch-1101ne]
  S1 = SWITCH-MOMENTARY-2 [package=tactile-switch-1101ne]
  S9 = SWITCH-MOMENTARY-2 [package=tactile-switch-1101ne]
  S14 = SWITCH-MOMENTARY-2 [package=tactile-switch-1101ne]
  S10 = SWITCH-MOMENTARY-2 [package=tactile-switch-1101ne]
  S6 = SWITCH-MOMENTARY-2 [package=tactile-switch-1101ne]
  S2 = SWITCH-MOMENTARY-2 [package=tactile-switch-1101ne]
  S3 = SWITCH-MOMENTARY-2 [package=tactile-switch-1101ne]
  S7 = SWITCH-MOMENTARY-2 [package=tactile-switch-1101ne]
  S11 = SWITCH-MOMENTARY-2 [package=tactile-switch-1101ne]
  S15 = SWITCH-MOMENTARY-2 [package=tactile-switch-1101ne]
  S16 = SWITCH-MOMENTARY-2 [package=tactile-switch-1101ne]
  S12 = SWITCH-MOMENTARY-2 [package=tactile-switch-1101ne]
  S8 = SWITCH-MOMENTARY-2 [package=tactile-switch-1101ne]
  S4 = SWITCH-MOMENTARY-2 [package=tactile-switch-1101ne]
  R1 = Resistor [tolerance=±5% resistance=10k package=THT]
  R2 = Resistor [tolerance=±5% resistance=10k package=THT]
  R3 = Resistor [tolerance=±5% resistance=10k package=THT]
  R4 = Resistor [tolerance=±5% resistance=10k package=THT]

nets:
  pin2: S5.1, S6.1, S7.1, S8.1
  N1: S5.2, S13.2, S1.2, S9.2, R1.Pin_0
  pin4: S13.1, S14.1, S15.1, S16.1
  pin1: S1.1, S2.1, S3.1, S4.1
  pin3: S9.1, S10.1, S11.1, S12.1
  N2: S14.2, S10.2, S6.2, S2.2, R2.Pin_0
  N3: S3.2, S7.2, S11.2, S15.2, R3.Pin_0
  N4: S16.2, S12.2, S8.2, S4.2, R4.Pin_0
  pin5: R1.Pin_1
  pin6: R2.Pin_1
  pin7: R3.Pin_1
  pin8: R4.Pin_1
