# Fritzing sketch 74hc244 (saved by Fritzing 0.9.3b)
perfboards: 1

parts:
  Part2 = QFN-20-0.4MM [chip_label=QFN-20-0.4MM package=QFN]
  R9 = Resistor [tolerance=±5% resistance=330 package=THT]
  R10 = Resistor [tolerance=±5% resistance=330 package=THT]
  R11 = Resistor [tolerance=±5% resistance=330 package=THT]
  R12 = Resistor [tolerance=±5% resistance=330 package=THT]
  R13 = Resistor [tolerance=±5% resistance=330 package=THT]
  R14 = Resistor [tolerance=±5% resistance=330 package=THT]
  R15 = Resistor [tolerance=±5% resistance=330 package=THT]
  R16 = Resistor [tolerance=±5% resistance=330 package=THT]

nets:
  1OE: Part2.1
  1A0: Part2.2
  2Y0: Part2.3, R13.Pin_1
  1A1: Part2.4
  2Y1: Part2.5, R12.Pin_1
  1A2: Part2.6
  2Y2: Part2.7, R11.Pin_1
  1A3: Part2.8
  2Y3: Part2.9, R10.Pin_1
  GND: Part2.10
  2A3: Part2.11
  1Y3: Part2.12, R14.Pin_1
  2A2: Part2.13
  1Y2: Part2.14, R15.Pin_1
  2A1: Part2.15
  1Y1: Part2.16, R9.Pin_1
  2A0: Part2.17
  1Y0: Part2.18, R16.Pin_1
  2OE: Part2.19
  5V: Part2.20
