# Fritzing sketch 74hc595Ledevices (saved by Fritzing 0.9.3b)
perfboards: 1

parts:
  U4 = 74HC595 [package="DIP16 [THT]"]
  U5 = 74HC595 [package="DIP16 [THT]"]
  U1 = 74HC595 [package="DIP16 [THT]"]

nets:
  D9: U4.Q1
  D10: U4.Q2
  D11: U4.Q3
  D12: U4.Q4
  D13: U4.Q5
  D14: U4.Q6
  D15: U4.Q7
  GND: U4.GND, U4.OE, U5.GND, U5.OE, U1.GND, U1.OE
  N1: U4.Q7', U5.DS
  5V: U4.MR, U4.VCC, U5.MR, U5.VCC, U1.MR, U1.VCC
  CLK: U4.SH_CP, U5.SH_CP, U1.SH_CP
  SCK: U4.ST_CP, U5.ST_CP, U1.ST_CP
  N2: U4.DS, U1.Q7'
  D8: U4.Q0
  D17: U5.Q1
  D18: U5.Q2
  D19: U5.Q3
  D20: U5.Q4
  D21: U5.Q5
  D22: U5.Q6
  D23: U5.Q7
  D16: U5.Q0
  D1: U1.Q1
  D2: U1.Q2
  D3: U1.Q3
  D4: U1.Q4
  D5: U1.Q5
  D6: U1.Q6
  D7: U1.Q7
  DA: U1.DS
  D0: U1.Q0
