# Fritzing sketch 8x8Led (saved by Fritzing 0.9.3b)
perfboards: 1

parts:
  Q1 = PNP-Transistor [package="TO92 [THT]"]
  Q2 = PNP-Transistor [package="TO92 [THT]"]
  Q3 = PNP-Transistor [package="TO92 [THT]"]
  Q5 = PNP-Transistor [package="TO92 [THT]"]
  Q6 = PNP-Transistor [package="TO92 [THT]"]
  Q7 = PNP-Transistor [package="TO92 [THT]"]
  Q8 = PNP-Transistor [package="TO92 [THT]"]
  Disp1 = LBT2088AH [part_number=LBT2088AH]
  Q9 = PNP-Transistor [package="TO92 [THT]"]

nets:
  5V: Q1.E, Q2.E, Q3.E, Q5.E, Q6.E, Q7.E, Q8.E, Q9.E
  LIN1: Q1.B
  N1: Q1.C, Disp1.pin_9
  LIN2: Q2.B
  N2: Q2.C, Disp1.pin_14
  LIN3: Q3.B
  N3: Q3.C, Disp1.pin_8
  LIN5: Q5.B
  N4: Q5.C, Disp1.pin1
  LIN6: Q6.B
  N5: Q6.C, Disp1.pin_7
  LIN7: Q7.B
  N6: Q7.C, Disp1.pin2
  LIN8: Q8.B
  N7: Q8.C, Disp1.pin_5
  N8: Disp1.pin_12, Q9.C
  LIN4: Q9.B
