# Fritzing sketch 51-MinimalSystem (saved by Fritzing 0.9.3b)
circuit board: 6.26862cm x 5.963cm
perfboards: 1

parts:
  S1 = Pushbutton [package=THT]
  C1 = Electrolytic Capacitor [capacitance=10pF part_number="30 pF" voltage=6.3V package="100 mil [THT, electrolytic]"]
  R1 = Resistor [tolerance=±5% resistance=10k package=THT]
  C4 = Ceramic Capacitor [capacitance=1µF package="100 mil [THT, multilayer]"]
  C2 = Electrolytic Capacitor [capacitance=0pF part_number="30 pF" package="100 mil [THT, electrolytic]"]
  U1 = STC89C52
  Y1 = CRYSTAL [part_number="11.52 MH" package=crystal-smd-10.5x4.8-2pin]

nets:
  N1: S1.leg0, R1.Pin_0, C4.0, U1.RST
  5V: S1.leg1, C4.1, U1.EN/, U1.VCC
  GND: C1.-, R1.Pin_1, C2.-, U1.GND
  N2: C1.+, U1.TXAL1, Y1.1
  N3: C2.+, U1.TXAL2, Y1.2

custom parts:
  STC89C52: MCU
